// Digital circuit RV5-PROCESSOR.dig as structural Verilog
module RV5_PROCESSOR (
  input  clock,
  input  in_2,
  input  in_3,
  input  in_4,
  input  in_6,
  input  clk,
  output [31:0] out_5
);

  wire abstractauto_wen, abstractcs_busy, abstractcs_wen, ack_drop, alu_mod, and_5_out, and_8_out,
       and_11_out, and_12_out, and_13_out, and_14_out, and_15_out, and_16_out, and_17_out, and_18_out,
       and_19_out, and_20_out, and_21_out, and_22_out, and_23_out, and_27_out, and_34_out, and_38_out,
       and_40_out, and_42_out, autoexec, br_cond, branch_sel, clk_t, command_exec,
       command_reg_aarpostincrement, command_reg_arg0wen, command_reg_exec, command_reg_jumpprogbuf,
       command_reg_postexec, command_reg_regnoinvalid, command_reg_regwen, command_reg_sel,
       command_reg_transfer, command_reg_validtransferex, command_reg_write, command_unsuported_sel,
       command_wen, comparator_2_eq, comparator_3_eq, comparator_4_eq, comparator_5_eq, comparator_6_eq,
       comparator_7_eq, comparator_8_eq, comparator_9_eq, comparator_10_eq, comparator_11_eq,
       comparator_12_gt, comparator_13_eq, comparator_15_gt, comparator_16_lt, comparator_18_lt,
       comparator_19_gt, comparator_20_eq, comparator_21_eq, comparator_22_eq, comparator_23_eq,
       comparator_24_eq, comparator_25_eq, comparator_26_eq, comparator_27_eq, comparator_28_eq,
       comparator_29_eq, comparator_30_eq, csr_opclear, csr_opset, csr_opwrite, csr_useimm, csr_wen,
       d_ff_2_q, d_ff_3_q, d_ff_4_q, d_ff_5_q, d_ff_7_nq, d_ff_8_q, d_ff_9_q, d_ff_10_q, dm_ack, dm_done,
       dm_start, dm_wen, dmcontrol_ackhavereset, dmcontrol_clrresethaltreq, dmcontrol_dmactive,
       dmcontrol_haltreq, dmcontrol_hartreset, dmcontrol_hasel, dmcontrol_ndmreset, dmcontrol_wen,
       dmi_access, dmi_ren, dmi_req, dmi_req_last_low, dmi_wen, dmstatus_allhalted, dmstatus_allnonexistent,
       dmstatus_allresumeack, dmstatus_allrunning, DPC194, dret_sel, ebreak_sel, ecall_sel, gdbserver_1_p2,
       gdbserver_1_p4, gdbserver_1_p5, gdbserver_1_p6, haltreq, I_imm_sel, jal_sel, jalr_sel, ld_signext,
       mret_sel, multiplexer_11_out, multiplexer_19_out, multiplexer_21_out, nor_1_out, nor_2_out, not_1_out,
       not_2_out, not_3_out, not_5_out, not_6_out, not_9_out, not_10_out, not_11_out, not_12_out, not_13_out,
       not_14_out, not_15_out, not_16_out, not_17_out, or_1_out, or_2_out, or_3_out, or_5_out, or_7_out,
       or_9_out, or_10_out, or_12_out, or_14_out, or_15_out, or_16_out, or_17_out, or_18_out, ram_b, ram_h,
       ram_ren, ram_wen, reg_wen, register_3_q, rising_edge_1_o, rising_edge_4_o, rs_ff_as_1_q,
       rv5_tap_1_dmi_req, rv5_tap_1_dmi_write, S_imm_sel, SB_imm_sel, sbcs_wen, stopcond, U_imm_sel,
       UJ_imm_sel;
  wire [1:0] alu_a_sel, wb_sel;
  wire [2:0] abstractcs_cmderr, alu_op, and_24_out, command_reg_aarsize, dmi_rdata_lut_out, dmi_wen_lut_out,
       funct3, multiplexer_2_out, multiplexer_5_out, not_7_out;
  wire [4:0] command_reg_gprno, multiplexer_16_out, multiplexer_17_out, multiplexer_18_out,
       multiplexer_20_out, rd, rs1, rs2;
  wire [6:0] funct7, opcode, rv5_tap_1_dmi_addr;
  wire [7:0] command_cmdtype;
  wire [11:0] abstractauto_autoexecdata, system_imm;
  wire [15:0] abstractauto_autoexecprogbuf, command_reg_regno;
  wire [15:5] sub_1_s;
  wire [15:12] abstractauto_persistent;
  wire [19:0] dmcontrol_hartsel;
  wire [23:23] multiplexer_10_out;
  wire [30:2] dmcontrol_persistent;
  wire [30:3] dmcontrol_rdata;
  wire [31:0] addr_dm, alu_out, and_25_out, command_persistent_q, csr_out, dcsr, dm_wdata, dmi_memaddr,
       dmi_rdata, dmi_wdata, dpc, imm_32, mem_out, mepc, mtvec, multiplexer_1_out, multiplexer_6_out,
       multiplexer_7_out, multiplexer_9_out, multiplexer_12_out, multiplexer_13_out, multiplexer_14_out,
       multiplexer_15_out, not_8_out, or_8_out, out_dm, ra, rb, rv5_memory_1_out_inst, rv5_pcu_1_pc;
  wire [31:2] nextpc;

  Register #(.Bits(32)) u_dmcontrol_persistent (
    .D(dmi_wdata), .C(clk_t), .en(dmcontrol_wen),
    .Q({dmcontrol_haltreq, dmcontrol_persistent[30], dmcontrol_hartreset, dmcontrol_persistent[28:27], dmcontrol_hasel, dmcontrol_hartsel[9:0], dmcontrol_hartsel[19:10], dmcontrol_persistent[5:2], dmcontrol_ndmreset, dmcontrol_dmactive}));
  and and_1 (dmcontrol_clrresethaltreq, dmcontrol_wen, dmi_wdata[2]);
  and and_2 (dmcontrol_rdata[3], dmcontrol_wen, dmi_wdata[3]);
  and and_3 (dmcontrol_ackhavereset, dmcontrol_wen, dmi_wdata[28]);
  and and_4 (dmcontrol_rdata[30], dmcontrol_wen, dmi_wdata[30]);
  D_FF d_ff_1 (.D(dmi_req), .C(clk_t), .nQ(dmi_req_last_low));  // open: Q
  and and_5 (and_5_out, dmcontrol_rdata[30], dcsr[2]);
  RISING_EDGE rising_edge_1 (.clk(clk_t), .d(dmi_req), .o(rising_edge_1_o));
  D_FF d_ff_2 (.D(and_5_out), .C(clk_t), .Q(d_ff_2_q));  // open: nQ
  D_FF d_ff_3 (.D(d_ff_2_q), .C(clk_t), .Q(d_ff_3_q));  // open: nQ
  nor nor_1 (nor_1_out, rising_edge_1_o, abstractcs_busy);
  D_FF d_ff_4 (.D(d_ff_3_q), .C(clk_t), .Q(d_ff_4_q));  // open: nQ
  RISING_EDGE rising_edge_2 (.clk(clk_t), .d(nor_1_out), .o(dm_done));
  or or_1 (or_1_out, dm_done, ack_drop);
  or or_2 (or_2_out, dmcontrol_haltreq, d_ff_4_q);
  and and_6 (dm_start, dmi_req, not_1_out);
  not not_1 (not_1_out, dm_ack);
  and and_7 (ack_drop, not_2_out, dm_ack);
  not not_2 (not_2_out, dmi_req);
  and and_8 (and_8_out, or_2_out, not_3_out);
  not not_3 (not_3_out, dmstatus_allhalted);
  Register register_1 (.D(dm_done), .C(clk_t), .en(or_1_out), .Q(dm_ack));
  RISING_EDGE rising_edge_3 (.clk(clk_t), .d(and_8_out), .o(haltreq));
  not not_4 (dmstatus_allrunning, dmstatus_allhalted);
  Comparator #(.Bits(20)) comparator_1 (
    .a(dmcontrol_hartsel), .b({20{1'b0}}), .gt(dmstatus_allnonexistent));  // open: eq, lt
  RS_FF rs_ff_1 (.S(dmcontrol_rdata[30]), .C(clk_t), .R(dmcontrol_haltreq), .Q(dmstatus_allresumeack));  // open: nQ
  // GdbServer gdbserver_1: pin names not known; wires that end beside it: clk, gdbserver_1_p2, clk_t, gdbserver_1_p4, gdbserver_1_p5, gdbserver_1_p6
  RV5_TAP rv5_tap_1 (
    .TCK(gdbserver_1_p4), .TMS(gdbserver_1_p5), .TDI(gdbserver_1_p6), .DMI_ACK(dm_ack),
    .DMI_RDATA(dmi_rdata), .DMI_STATUS({2{abstractcs_busy}}), .TDO(gdbserver_1_p2),
    .DMI_REQ(rv5_tap_1_dmi_req), .DMI_WDATA(dmi_wdata), .DMI_ADDR(rv5_tap_1_dmi_addr),
    .DMI_WRITE(rv5_tap_1_dmi_write));
  RISING_EDGE rising_edge_4 (.clk(clk_t), .d(dmi_req), .o(rising_edge_4_o));
  Comparator #(.Bits(32)) comparator_2 (.a(dmi_memaddr), .b(32'hffc), .eq(comparator_2_eq));  // open: gt, lt
  Comparator #(.Bits(32)) comparator_3 (.a(dmi_memaddr), .b(32'h1004), .eq(comparator_3_eq));  // open: gt, lt
  Comparator #(.Bits(32)) comparator_4 (.a(dmi_memaddr), .b(32'h1008), .eq(comparator_4_eq));  // open: gt, lt
  Comparator #(.Bits(32)) comparator_5 (.a(dmi_memaddr), .b(32'h100c), .eq(comparator_5_eq));  // open: gt, lt
  Comparator #(.Bits(32)) comparator_6 (.a(dmi_memaddr), .b(32'h1010), .eq(comparator_6_eq));  // open: gt, lt
  Comparator #(.Bits(32)) comparator_7 (.a(dmi_memaddr), .b(32'h1014), .eq(comparator_7_eq));  // open: gt, lt
  Comparator #(.Bits(32)) comparator_8 (.a(dmi_memaddr), .b(32'h1018), .eq(comparator_8_eq));  // open: gt, lt
  Comparator #(.Bits(32)) comparator_9 (.a(dmi_memaddr), .b(32'h101c), .eq(comparator_9_eq));  // open: gt, lt
  Comparator #(.Bits(32)) comparator_10 (.a(dmi_memaddr), .b(32'h1020), .eq(comparator_10_eq));  // open: gt, lt
  D_FF d_ff_5 (.D(rv5_tap_1_dmi_req), .C(clk_t), .Q(d_ff_5_q));  // open: nQ
  and and_9 (dmi_wen, rv5_tap_1_dmi_write, rising_edge_4_o);
  and and_10 (dmi_ren, not_5_out, rising_edge_4_o);
  not not_5 (not_5_out, rv5_tap_1_dmi_write);
  and and_11 (and_11_out, comparator_2_eq, dmi_access, abstractauto_autoexecdata[0]);
  and and_12 (and_12_out, comparator_3_eq, dmi_access, abstractauto_autoexecprogbuf[0]);
  and and_13 (and_13_out, comparator_4_eq, dmi_access, abstractauto_autoexecprogbuf[1]);
  and and_14 (and_14_out, comparator_5_eq, dmi_access, abstractauto_autoexecprogbuf[2]);
  and and_15 (and_15_out, comparator_6_eq, dmi_access, abstractauto_autoexecprogbuf[3]);
  and and_16 (and_16_out, comparator_7_eq, dmi_access, abstractauto_autoexecprogbuf[4]);
  and and_17 (and_17_out, comparator_8_eq, dmi_access, abstractauto_autoexecprogbuf[5]);
  and and_18 (and_18_out, comparator_9_eq, dmi_access, abstractauto_autoexecprogbuf[6]);
  and and_19 (and_19_out, comparator_10_eq, dmi_access, abstractauto_autoexecprogbuf[7]);
  D_FF d_ff_6 (.D(d_ff_5_q), .C(clk_t), .Q(dmi_req));  // open: nQ
  or or_3 (or_3_out, dmi_ren, dmi_wen);
  and and_20 (and_20_out, or_3_out, dmi_req);
  or or_4 (autoexec, and_11_out, and_12_out, and_13_out, and_14_out, and_15_out, and_16_out, and_17_out, and_18_out, and_19_out);
  RISING_EDGE rising_edge_5 (.clk(clk_t), .d(and_20_out), .o(dmi_access));
  LookUpTable #(.Bits(3)) dmi_rdata_lut (
    .in0(rv5_tap_1_dmi_addr[0]), .in1(rv5_tap_1_dmi_addr[1]), .in2(rv5_tap_1_dmi_addr[2]),
    .in3(rv5_tap_1_dmi_addr[3]), .in4(rv5_tap_1_dmi_addr[4]), .in5(rv5_tap_1_dmi_addr[5]),
    .in6(rv5_tap_1_dmi_addr[6]), .out(dmi_rdata_lut_out));
  LookUpTable #(.Bits(3)) dmi_wen_lut (
    .in0(rv5_tap_1_dmi_addr[0]), .in1(rv5_tap_1_dmi_addr[1]), .in2(rv5_tap_1_dmi_addr[2]),
    .in3(rv5_tap_1_dmi_addr[3]), .in4(rv5_tap_1_dmi_addr[4]), .in5(rv5_tap_1_dmi_addr[5]),
    .in6(rv5_tap_1_dmi_addr[6]), .out(dmi_wen_lut_out));
  LookUpTable #(.Bits(32)) dmi_memaddr_lut (
    .in0(rv5_tap_1_dmi_addr[0]), .in1(rv5_tap_1_dmi_addr[1]), .in2(rv5_tap_1_dmi_addr[2]),
    .in3(rv5_tap_1_dmi_addr[3]), .in4(rv5_tap_1_dmi_addr[4]), .in5(rv5_tap_1_dmi_addr[5]),
    .in6(rv5_tap_1_dmi_addr[6]), .out(dmi_memaddr));
  and and_21 (and_21_out, command_reg_regnoinvalid, command_reg_transfer);
  Multiplexer #(.Selector_Bits(3), .Bits(32)) multiplexer_1 (
    .sel(dmi_rdata_lut_out), .in_0({32{1'b0}}), .in_1(out_dm),
    .in_2({dmcontrol_haltreq, dmcontrol_rdata[30], dmcontrol_hartreset, dmcontrol_ackhavereset, 1'b0, dmcontrol_hasel, dmcontrol_hartsel[9:0], dmcontrol_hartsel[19:10], 2'b00, dmcontrol_rdata[3], dmcontrol_clrresethaltreq, dmcontrol_ndmreset, dmcontrol_dmactive}),
    .in_3({{14{1'b0}}, {2{dmstatus_allresumeack}}, {2{dmstatus_allnonexistent}}, 2'b00, {2{dmstatus_allrunning}}, {2{dmstatus_allhalted}}, 8'h82}),
    .in_4(32'h111ffc), .in_5({19'h4000, abstractcs_busy, 1'b0, abstractcs_cmderr, 8'h1}),
    .in_6(32'h20000000), .in_7({abstractauto_autoexecprogbuf, 4'b0000, abstractauto_autoexecdata}),
    .out(multiplexer_1_out));
  Demultiplexer #(.Selector_Bits(3)) demultiplexer_1 (
    .sel(dmi_wen_lut_out), .in(dmi_wen), .out_1(dmcontrol_wen), .out_2(abstractcs_wen), .out_3(command_wen),
    .out_4(sbcs_wen), .out_5(abstractauto_wen));  // open: out_0, out_6, out_7
  Comparator #(.Bits(32)) comparator_11 (.a(dmi_memaddr), .b({32{1'b0}}), .eq(comparator_11_eq));  // open: gt, lt
  and and_22 (and_22_out, dmi_ren, dmi_req, dmi_req_last_low);
  not not_6 (not_6_out, comparator_11_eq);
  Comparator #(.Bits(3)) comparator_12 (.a(command_reg_aarsize), .b(3'b010), .gt(comparator_12_gt));  // open: eq, lt
  Register #(.Bits(32)) register_2 (.D(multiplexer_1_out), .C(clk_t), .en(and_22_out), .Q(dmi_rdata));
  and and_23 (and_23_out, dmi_wen, not_6_out);
  or or_5 (or_5_out, command_unsuported_sel, comparator_12_gt, and_21_out, command_reg_aarpostincrement);
  Multiplexer #(.Bits(3)) multiplexer_2 (.sel(or_5_out), .in_0(3'b000), .in_1(3'b010), .out(multiplexer_2_out));
  Multiplexer #(.Bits(32)) multiplexer_3 (.sel(command_reg_arg0wen), .in_0(dmi_wdata), .in_1(ra), .out(dm_wdata));
  or or_6 (dm_wen, and_23_out, command_reg_arg0wen);
  Multiplexer #(.Bits(32)) multiplexer_4 (
    .sel(command_reg_validtransferex), .in_0(dmi_memaddr), .in_1(32'hffc), .out(addr_dm));
  assign and_24_out = not_7_out & abstractcs_cmderr;  // And and_24, 3 bits wide
  assign not_7_out = ~dmi_wdata[10:8];  // Not not_7, 3 bits wide
  Multiplexer #(.Bits(3)) multiplexer_5 (
    .sel(command_reg_exec), .in_0(and_24_out), .in_1(multiplexer_2_out), .out(multiplexer_5_out));
  or or_7 (or_7_out, abstractcs_wen, command_exec);
  Register #(.Bits(3)) u_abstractcs_cmderr (.D(multiplexer_5_out), .C(clk_t), .en(or_7_out), .Q(abstractcs_cmderr));
  Multiplexer #(.Bits(32)) multiplexer_6 (
    .sel(csr_useimm), .in_0(ra), .in_1({{27{1'b0}}, rs1}), .out(multiplexer_6_out));
  assign and_25_out = not_8_out & csr_out;  // And and_25, 32 bits wide
  assign not_8_out = ~multiplexer_6_out;  // Not not_8, 32 bits wide
  assign or_8_out = multiplexer_6_out | csr_out;  // Or or_8, 32 bits wide
  Multiplexer #(.Bits(32)) multiplexer_7 (
    .sel(csr_opclear), .in_0(multiplexer_6_out), .in_1(and_25_out), .out(multiplexer_7_out));
  Multiplexer multiplexer_8 (.sel(or_9_out), .in_0(clock), .in_1(in_2), .out(clk_t));
  RV5_PCU rv5_pcu_1 (
    .IMM_32(imm_32), .CLK(clk_t), .IS_BRANCH(branch_sel), .IS_JAL(jal_sel), .IS_JALR(jalr_sel),
    .COND_MET(br_cond), .ALU_OUT(alu_out), .IS_ECALL(ecall_sel), .MTVEC(mtvec), .MEPC(mepc),
    .IS_MRET(mret_sel), .IS_EBREAK(ebreak_sel), .IS_DEBUG(dmstatus_allhalted), .DCSR(dcsr), .DPC(dpc),
    .IS_DRET(dret_sel), .HALTREQ(haltreq), .JUMPPROGBUF(command_reg_jumpprogbuf),
    .RESUMEREQ(dmcontrol_rdata[30]), .PC(rv5_pcu_1_pc));
  Multiplexer #(.Bits(32)) multiplexer_9 (
    .sel(csr_opset), .in_0(multiplexer_7_out), .in_1(or_8_out), .out(multiplexer_9_out));
  or or_9 (or_9_out, in_3, stopcond);
  Register #(.Bits(32)) command_persistent (.D(dmi_wdata), .C(clk_t), .en(command_wen), .Q(command_persistent_q));
  Comparator #(.Bits(32)) comparator_13 (.a(rv5_pcu_1_pc), .b(32'h190), .eq(comparator_13_eq));  // open: gt, lt
  Comparator #(.Bits(32)) comparator_14 (.a(rv5_pcu_1_pc), .b(32'h194), .eq(DPC194));  // open: gt, lt
  Comparator #(.Bits(32)) comparator_15 (.a(rv5_pcu_1_pc), .b(32'h1003), .gt(comparator_15_gt));  // open: eq, lt
  Comparator #(.Bits(32)) comparator_16 (.a(rv5_pcu_1_pc), .b(32'h1021), .lt(comparator_16_lt));  // open: gt, eq
  D_FF d_ff_7 (.D(command_wen), .C(clk_t), .nQ(d_ff_7_nq));  // open: Q
  RV5_IMM rv5_imm_1 (
    .UJ_imm_sel(UJ_imm_sel), .I_imm_sel(I_imm_sel), .SB_imm_sel(SB_imm_sel), .S_imm_sel(S_imm_sel),
    .U_imm_sel(U_imm_sel), .INSTR_32(rv5_memory_1_out_inst), .imm(imm_32));
  Add #(.Bits(30)) add_1 (.a(rv5_pcu_1_pc[31:2]), .b({30{1'b0}}), .c_i(1'b1), .s(nextpc));  // open: c_o
  RV5_CSR rv5_csr_1 (
    .clk(clk_t), .addr(system_imm), .w_data(multiplexer_9_out), .wen(csr_wen), .pc_in(rv5_pcu_1_pc),
    .ecall_sel(ecall_sel), .mret_sel(mret_sel), .ebreak_sel(ebreak_sel), .is_debug(dmstatus_allhalted),
    .haltreq(haltreq), .R_DATA(csr_out), .MTVEC_OUT(mtvec), .MEPC_OUT(mepc), .DCSR_OUT(dcsr), .DPC_OUT(dpc));
  or or_10 (or_10_out, comparator_13_eq, DPC194);
  and and_26 (abstractcs_busy, comparator_15_gt, comparator_16_lt);
  and and_27 (and_27_out, d_ff_7_nq, command_wen);
  nor nor_2 (nor_2_out, abstractcs_cmderr[0], abstractcs_cmderr[1], abstractcs_cmderr[2]);
  Comparator #(.Bits(8)) comparator_17 (
    .a(command_cmdtype), .b({8{1'b0}}), .gt(command_unsuported_sel), .eq(command_reg_sel));  // open: lt
  and and_28 (command_reg_exec, command_exec, command_reg_sel);
  Comparator #(.Bits(16)) comparator_18 (.a(command_reg_regno), .b(16'h1000), .lt(comparator_18_lt));  // open: gt, eq
  Comparator #(.Bits(16)) comparator_19 (.a(command_reg_regno), .b(16'h101f), .gt(comparator_19_gt));  // open: eq, lt
  or or_11 (dmstatus_allhalted, or_10_out, abstractcs_busy);
  Multiplexer #(.Bits(32)) multiplexer_10 (
    .sel(and_27_out), .in_0(command_persistent_q), .in_1(dmi_wdata),
    .out({command_cmdtype, multiplexer_10_out[23], command_reg_aarsize, command_reg_aarpostincrement, command_reg_postexec, command_reg_transfer, command_reg_write, command_reg_regno}));
  or or_12 (or_12_out, command_wen, autoexec);
  RV5_INSTR_DECODE rv5_instr_decode_1 (
    .instr(rv5_memory_1_out_inst), .funct7(funct7), .rs2(rs2), .rs1(rs1), .funct3(funct3), .rd(rd),
    .opcode(opcode), .UJ_imm_sel(UJ_imm_sel), .U_imm_sel(U_imm_sel), .S_imm_sel(S_imm_sel),
    .SB_imm_sel(SB_imm_sel), .I_imm_sel(I_imm_sel), .alu_mod(alu_mod), .ram_wen(ram_wen), .wb_sel(wb_sel),
    .ram_ren(ram_ren), .ecall_sel(ecall_sel), .alu_op(alu_op), .ram_b(ram_b), .ram_h(ram_h),
    .reg_wen(reg_wen), .branch_sel(branch_sel), .jal_sel(jal_sel), .jalr_sel(jalr_sel),
    .alu_a_sel(alu_a_sel), .ld_signext(ld_signext), .csr_wen(csr_wen), .mret_sel(mret_sel),
    .system_imm(system_imm), .ebreak_sel(ebreak_sel), .dret_sel(dret_sel), .csr_opwrite(csr_opwrite),
    .csr_opset(csr_opset), .csr_opclear(csr_opclear), .csr_useimm(csr_useimm));
  or or_13 (command_reg_regnoinvalid, comparator_18_lt, comparator_19_gt);
  and and_29 (command_exec, or_12_out, nor_2_out);
  Multiplexer multiplexer_11 (.sel(haltreq), .in_0(ram_wen), .in_1(1'b0), .out(multiplexer_11_out));
  Multiplexer #(.Selector_Bits(2), .Bits(32)) multiplexer_12 (
    .sel(alu_a_sel), .in_0(ra), .in_1(rv5_pcu_1_pc), .in_2({32{1'b0}}), .in_3({32{1'b0}}),
    .out(multiplexer_12_out));
  Multiplexer #(.Bits(32)) multiplexer_13 (.sel(or_14_out), .in_0(rb), .in_1(imm_32), .out(multiplexer_13_out));
  or or_14 (or_14_out, I_imm_sel, S_imm_sel, U_imm_sel);
  RV5_MEMORY rv5_memory_1 (
    .addr(alu_out), .wdata(rb), .wen(multiplexer_11_out), .ren(ram_ren), .clk(clk_t), .\byte (ram_b),
    .half(ram_h), .signext(ld_signext), .addr_inst(rv5_pcu_1_pc), .addr_dm(addr_dm), .wen_dm(dm_wen),
    .wdata_dm(dm_wdata), .out(mem_out), .out_inst(rv5_memory_1_out_inst), .out_dm(out_dm), .d0O(out_5));
  RV5_ALU rv5_alu_1 (
    .OP(alu_op), .Y(alu_out), .A(multiplexer_12_out), .B(multiplexer_13_out), .BR(br_cond), .MOD(alu_mod));
  Multiplexer #(.Selector_Bits(2), .Bits(32)) multiplexer_14 (
    .sel(wb_sel), .in_0(alu_out), .in_1({nextpc, 2'b00}), .in_2(mem_out), .in_3(csr_out),
    .out(multiplexer_14_out));
  not not_9 (not_9_out, command_reg_regnoinvalid);
  and and_30 (command_reg_arg0wen, not_10_out, command_reg_validtransferex);
  not not_10 (not_10_out, command_reg_write);
  and and_31 (command_reg_regwen, command_reg_write, command_reg_validtransferex);
  Sub #(.Bits(16)) sub_1 (
    .a(command_reg_regno), .b(16'h1000), .c_i(1'b0), .s({sub_1_s, command_reg_gprno}));  // open: c_o
  and and_32 (command_reg_jumpprogbuf, command_reg_postexec, command_reg_exec);
  and and_33 (command_reg_validtransferex, command_reg_exec, command_reg_transfer, not_9_out);
  Multiplexer #(.Bits(32)) multiplexer_15 (
    .sel(command_reg_exec), .in_0(multiplexer_14_out), .in_1(out_dm), .out(multiplexer_15_out));
  Multiplexer #(.Bits(5)) multiplexer_16 (.sel(ecall_sel), .in_0(rs1), .in_1(5'b01010), .out(multiplexer_16_out));
  Multiplexer #(.Bits(5)) multiplexer_17 (
    .sel(command_reg_exec), .in_0(multiplexer_16_out), .in_1(command_reg_gprno), .out(multiplexer_17_out));
  Multiplexer #(.Bits(5)) multiplexer_18 (.sel(ecall_sel), .in_0(rs2), .in_1(5'b10001), .out(multiplexer_18_out));
  or or_15 (or_15_out, reg_wen, command_reg_regwen);
  Multiplexer multiplexer_19 (.sel(haltreq), .in_0(or_15_out), .in_1(1'b0), .out(multiplexer_19_out));
  Register #(.Bits(32)) u_abstractauto_persistent (
    .D(dmi_wdata), .C(clk_t), .en(abstractauto_wen),
    .Q({abstractauto_autoexecprogbuf, abstractauto_persistent, abstractauto_autoexecdata}));
  Multiplexer #(.Bits(5)) multiplexer_20 (
    .sel(command_reg_regwen), .in_0(rd), .in_1(command_reg_gprno), .out(multiplexer_20_out));
  RV5_GPR rv5_gpr_1 (
    .RS1(multiplexer_17_out), .RS2(multiplexer_18_out), .D_in(multiplexer_15_out), .clk(clk_t),
    .WEN(multiplexer_19_out), .RD(multiplexer_20_out), .RA(ra), .RB(rb));  // open: RD0
  D_FF d_ff_8 (.D(command_exec), .C(clk_t), .Q(d_ff_8_q));  // open: nQ
  and and_34 (and_34_out, command_exec, command_reg_transfer);
  or or_16 (or_16_out, command_exec, d_ff_8_q);
  Comparator #(.Bits(32)) comparator_20 (.a(dm_wdata), .b({32{1'b0}}), .eq(comparator_20_eq));  // open: gt, lt
  not not_11 (not_11_out, comparator_20_eq);
  not not_12 (not_12_out, and_34_out);
  Comparator #(.Bits(32)) comparator_21 (.a(dmi_memaddr), .b(32'hffc), .eq(comparator_21_eq));  // open: gt, lt
  Comparator #(.Bits(32)) comparator_22 (.a(out_dm), .b({32{1'b0}}), .eq(comparator_22_eq));  // open: gt, lt
  Comparator #(.Bits(16)) comparator_23 (.a(command_reg_regno), .b(16'h1008), .eq(comparator_23_eq));  // open: gt, lt
  Comparator #(.Bits(12)) comparator_24 (.a(12'h7b0), .b(system_imm), .eq(comparator_24_eq));  // open: gt, lt
  not not_13 (not_13_out, comparator_22_eq);
  Comparator #(.Bits(32)) comparator_25 (.a(addr_dm), .b(32'h1024), .eq(comparator_25_eq));  // open: gt, lt
  // And and_35 has open pins: In_1=not_11_out, In_2=dm_wen, In_3=not_12_out, In_4=comparator_21_eq, out=open
  // And and_36 has open pins: In_1=comparator_21_eq, In_2=not_13_out, out=open
  Comparator #(.Bits(32)) comparator_26 (
    .a({abstractauto_autoexecprogbuf, 4'b0000, abstractauto_autoexecdata}), .b({32{1'b0}}),
    .eq(comparator_26_eq));  // open: gt, lt
  // And and_37 has open pins: In_1=comparator_24_eq, In_2=csr_wen, out=open
  and and_38 (and_38_out, comparator_23_eq, command_reg_write, 1'b1, command_reg_transfer, or_16_out);
  not not_14 (not_14_out, comparator_26_eq);
  // And and_39 has open pins: In_1=comparator_25_eq, In_2=dm_wen, In_3=dmi_wdata[2], out=open
  Comparator #(.Bits(32)) comparator_27 (.a(dm_wdata), .b({32{1'b0}}), .eq(comparator_27_eq));  // open: gt, lt
  Comparator #(.Bits(32)) comparator_28 (.a(out_5), .b({32{1'b0}}), .eq(comparator_28_eq));  // open: gt, lt
  Comparator #(.Bits(32)) comparator_29 (.a(out_5), .b({32{1'b0}}), .eq(comparator_29_eq));  // open: gt, lt
  RS_FF_AS rs_ff_as_1 (.S(autoexec), .R(1'b0), .Q(rs_ff_as_1_q));  // open: nQ
  Comparator #(.Bits(32)) comparator_30 (.a(addr_dm), .b(32'hffc), .eq(comparator_30_eq));  // open: gt, lt
  not not_15 (not_15_out, comparator_28_eq);
  not not_16 (not_16_out, comparator_29_eq);
  D_FF d_ff_9 (.D(in_4), .C(clk_t), .Q(d_ff_9_q));  // open: nQ
  D_FF d_ff_10 (.D(not_16_out), .C(clk_t), .Q(d_ff_10_q));  // open: nQ
  Comparator #(.Bits(3)) comparator_31 (.a(abstractcs_cmderr), .b(3'b111));  // open: gt, eq, lt
  not not_17 (not_17_out, d_ff_9_q);
  and and_40 (and_40_out, dm_wen, comparator_27_eq, comparator_30_eq, not_15_out);
  // And and_41 has open pins: In_1=comparator_29_eq, In_2=d_ff_10_q, out=open
  and and_42 (and_42_out, not_17_out, in_4);
  Multiplexer multiplexer_21 (.sel(in_4), .in_0(1'b0), .in_1(1'b0), .out(multiplexer_21_out));
  or or_17 (or_17_out, 1'b0, and_42_out);
  Register register_3 (.D(multiplexer_21_out), .C(clk_t), .en(or_17_out), .Q(register_3_q));
  or or_18 (or_18_out, 1'b0, register_3_q);
  and and_43 (stopcond, or_18_out, in_6);

  // Other names for the same wires on the sheet: abstractauto_persistent (some bits) = {abstractauto_autoexecprogbuf, abstractauto_autoexecdata};
  //   abstractauto_rdata (some bits) = {abstractauto_autoexecprogbuf, abstractauto_autoexecdata};
  //   abstractcs_rdata (some bits) = {abstractcs_busy, abstractcs_cmderr}; d0O[31:0] = out_5;
  //   dmcontrol_rdata (some bits) = {dmcontrol_haltreq, dmcontrol_hartreset, dmcontrol_ackhavereset, dmcontrol_hasel, dmcontrol_hartsel[9:0], dmcontrol_hartsel[19:10], dmcontrol_clrresethaltreq, dmcontrol_ndmreset, dmcontrol_dmactive};
  //   dmcontrol_persistent (some bits) = {dmcontrol_haltreq, dmcontrol_hartreset, dmcontrol_hasel, dmcontrol_hartsel[9:0], dmcontrol_hartsel[19:10], dmcontrol_ndmreset, dmcontrol_dmactive};
  //   dmcontrol_hartselhi[9:0] = dmcontrol_hartsel[19:10]; dmcontrol_hartsello[9:0] = dmcontrol_hartsel[9:0];
  //   dmcontrol_resumereq = dmcontrol_rdata[30]; dmcontrol_setresethaltreq = dmcontrol_rdata[3];
  //   dmstatus_anynonexistent = dmstatus_allnonexistent;
  //   dmstatus_rdata (some bits) = {{2{dmstatus_allresumeack}}, {2{dmstatus_allnonexistent}}, {2{dmstatus_allrunning}}, {2{dmstatus_allhalted}}};
  //   dmstatus_anyresumeack = dmstatus_allresumeack; dmstatus_anyrunning = dmstatus_allrunning;
  //   in_progbuf = abstractcs_busy; dmstatus_anyhalted = dmstatus_allhalted; is_debug = dmstatus_allhalted

  // Notes on the sheet:
  //   clock: Hz: 2147483647
  //   in_6: default 1
  //   clk: Hz: 50000
  //   Debug module registers:
  //   dmcontrol
  //   We store any fields that need to be
  //   persistent in a register:
  //   Every RW field can be directly
  //   extracted for use from the
  //   persistent register:
  //   W1 fields should only be high
  //   for the clock cycle that they're written:
  //   temp stuff
  //   It's useful to have each field separate
  //   for implementing their functionality,
  //   but let's also pack them up
  //   so that the debugger can read them:
  //   (And for convenience, let's 
  //   also expose this:)
  //   Additional debug module logic:
  //   halting
  //   We should halt if we're being asked to via dmcontrol or if we've just completed
  //   a single-step:
  //   Debug park loop > dret
  //   sbcs
  //   We don't support system bus
  //   access, so we can treat this entire
  //   register as effectively read-only:
  //   (We can get away with a hardcoded
  //   number of clock cycles for single-step.)
  //   dret > curr. instr
  //   curr. instr > next instr
  //   dmstatus
  //   Every field in mstatus is read-only.
  //   We know our CPU handles halts in a
  //   single clock cycle, so to avoid complication
  //   we won't hold this signal high.
  //   Determine each field's value:
  //   autoexec
  //   We just check if we're accessing any data/progbuf words
  //   that we're supposed to autoexec on access of:
  //   Pack them up so the debugger
  //   can read them:
  //   TODO: Simplify
  //   Are we reading or writing to dmi
  //   on this clock cycle?
  //   abstractcs
  //   contents of dmi_rdata_lut (hex, n*v repeats v):
  //   4*0,1,11*0,2,3,4,0,0,0,5,0,7,7*0,8*1,16*0,6
  //   contents of dmi_wen_lut (hex, n*v repeats v):
  //   16*0,1,5*0,2,3,5,31*0,4
  //   contents of dmi_memaddr_lut (hex, n*v repeats v):
  //   4*0,ffc,27*0,1004,1008,100c,1010,1014,1018,101c,1020
  //   Determine each field's value:
  //   (especially cmderr...)
  //   memory access
  //   If the debug module is accessing RAM,
  //   it is either because one of the dmi
  //   registers is memory-mapped, or 
  //   we are executing a command that
  //   requires us to do so.
  //   hartinfo
  //   command
  //   This is a write-only register. 
  //   We choose to process it entirely on the same cycle it is written.
  //   I should mention that we only implement the access register
  //   command. This is because it contains functionality for arbitrary
  //   code execution, which allows us to do everything else.
  //   Handle persistence and extract all fields:
  //   Figure out if we should be executing
  //   the command:
  //   Split out cmdtype to selectors:
  //   Determine if we need to execute a register access
  //   command:
  //   Figure out if regno is invalid:
  //   For now, address range check is
  //   the most robust way to know if
  //   we're in debug mode.
  //   Might change so debug ROM length
  //   is variable, but for now I KNOW this
  //   works.
  //   Determine if a valid transfer is to be executed:
  //   Will we end up reading a register?
  //   Let's see:
  //   What about writing?
  //   If we end up reading or writing a
  //   register, we'll need its number in
  //   the standard format:
  //   And finally figure out if we need to
  //   jump to the progbuf:
  //   abstractauto
  //   This is an optional register, but OpenOCD
  //   is bugged and requires it. (riscv-collab/riscv-openocd/issues/587)
  //   Store for persistence:
  //   Extract the fields:
  //   Debug stuff
  //   Pack up:
  //   Here we are trying to make this circuit hierarchical
  //       RV5-REGS contains register bank related hw.
  //       RV5-ALU contains ALU related hw
  //       RV5-INSTR-DECODE contains Instruction Reg, and all needed decodes
  //             decoder for immediate sel
  //       RV5-IMM is a combinatorial that extracts the needed immediates, 
  //              and provides the sign-extended 32-bit value thru a MUX.
  //       RV5-PCU needs some fixes.
  //              increments the PC and allows Jumps, and provides next PC for JAL save of PC.
  //   See examples in Digital in particular processors as to how 
  //   to do this.  
  //   TODO: 
  //   1st. Add a test to each element in the hierarchy.
  //   2nd Resize boxes with appropriate SVG for readable packages w. appropriate signals.
  //   We need to:
  //       RV5-INSTR-DECODE: Decodes the instruction set and provides control signals, and FMT
  //            decode for immediate select has been completed.
  //       Implement:
  //            RV5-LOAD-STORE: Provides Load and Store
  //            RV5-MEMORY: Include ROM and RAM.
  //            RV5-IO: Provides a mean to read a program, communicate with a terminal (keyboard/display)
  //            Create a ROM/RAM  bootstrap
  //                 that loads a program.
  //   Note: Assembler test programs can be found at:   
  //      https://github.com/riscv-software-src/riscv-tests
  //   PCU (Program Control Unit, 
  //   PC = PC + 4, or PC = PC += SBimm32
  //   or PC = ALU out or PC += sgn_ext-imm32
  //   for FMT U, and UJ
  //   Need to figure out a way to load memory
  //   with instructions, ideally from RARS.
  //   Check out how MARS does it for MIPS.
  //   NEXT, NEED LOAD AND STORE,
  //   Address comes from ALU output
  //   which goes to memory via see-thru latch
  //    latch,which goes out to memory for 
  //   loading and storing.  reads 32-word
  //   and stores in rd.   Need to figure out a good
  //   approach to read and write to memory 
  //   with Digital and load it at start up.
  //   We need to arbitrate use of memory 
  //   between load/store and fetching instruction.
  //   RV5-DECODER:
  //      decodes: opcode, funct3, funct7
  //      generates: 
  //           # FMT - DO I NEED IT HERE?
  //           # imm_sel,  DONE ALREADY
  //           wen, 
  //           sub/add, 
  //           func_sel
endmodule
